# Fritzing sketch Servo_Test (saved by Fritzing 0.9.3b)
breadboards: 1

parts:
  Part1 = Arduino Uno (Rev3)
  J1 = Basic Servo

nets:
  N1: Part1.D10_PWM/SS, J1.pulse
  5V: Part1.5V, J1.vcc
  GND: Part1.GND, J1.gnd
